# Fritzing sketch groovebox_nano_2 (saved by Fritzing 0.9.3b)
circuit board: 8.46667cm x 5.64444cm
breadboards: 1

parts:
  Εξάρτημα2 = OLED Monochrome 128x64 0.96 inch [part_number=326]
  Εξάρτημα1 = Arduino Nano (Rev3.0)
  ENCODER1 = Rotary Encoder with Knob
  ENCODER2 = Rotary Encoder with Knob
  S1 = SWITCH-MOMENTARY-2 [package=tactile-pth]
  S2 = SWITCH-MOMENTARY-2 [package=tactile-pth]
  S3 = SWITCH-MOMENTARY-2 [package=tactile-pth]
  S4 = SWITCH-MOMENTARY-2 [package=tactile-pth]
  S5 = SWITCH-MOMENTARY-2 [package=tactile-pth]
  S6 = SWITCH-MOMENTARY-2 [package=tactile-pth]
  U1 = 3.5mm Audio Jack [package=audio-jack]

nets:
  N1: Εξάρτημα2.MOSI_SDA, Εξάρτημα1.D8
  N2: Εξάρτημα2.SCLK_SCK, Εξάρτημα1.D10
  N3: Εξάρτημα2.DC_SA0, Εξάρτημα1.D11/MOSI
  N4: Εξάρτημα2.RESET, Εξάρτημα1.D13/SCK
  VIN: Εξάρτημα2.VIN, Εξάρτημα1.5V
  GND: Εξάρτημα2.GND, Εξάρτημα1.GND, ENCODER1.no_name_yet#2, ENCODER1.no_name_yet#4, ENCODER2.no_name_yet#2, ENCODER2.no_name_yet#4, U1.SLEEVE
  N5: Εξάρτημα1.D2, S5.1
  N6: Εξάρτημα1.D3, U1.RIGHT, U1.LEFT
  N7: Εξάρτημα1.D4, S4.1
  N8: Εξάρτημα1.D5, S3.1
  N9: Εξάρτημα1.D6, ENCODER2.no_name_yet#5
  N10: Εξάρτημα1.D7, ENCODER1.no_name_yet#5
  N11: Εξάρτημα1.D9, S2.1
  N12: Εξάρτημα1.D12/MISO, S1.1
  N13: Εξάρτημα1.A4, S6.2
  N14: Εξάρτημα1.A3, ENCODER1.no_name_yet#1
  N15: Εξάρτημα1.A2, ENCODER1.no_name_yet#3
  N16: Εξάρτημα1.A1, ENCODER2.no_name_yet#1
  N17: Εξάρτημα1.A0, ENCODER2.no_name_yet#3

custom parts:
  OLED Monochrome 128x64 0.96 inch: These displays are small, only about 1" diameter, but very readable due to the high contrast of an OLED display. This display is made of 128x64 individual white OLED pixels, each one is turned on or off by the controller chip. Because the display makes its own light, no backlight is required. This reduces the power required to run the OLED and is why the display has such high contrast; we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
  Rotary Encoder with Knob: Rotary Encoder with 1/4" Shaft and Knob
